// Logisim project MIPS-4bit-G2 - Hardware - V2.circ as structural Verilog: 8 circuits, main circuit main
// 1
module main (
  input  RESET,
  output [3:0] Z,
  output [3:0] t0,
  output [3:0] t1,
  output [3:0] t2,
  output [3:0] t3,
  output [3:0] t4
);

  wire clock_1_out, control_1_alusrc_3, control_1_beq_5, control_1_bneq_4, control_1_jump_11,
       control_1_memread_8, control_1_memtoreg_6, control_1_memwrit_7, control_1_regdst_10,
       control_1_regwrite_9, n4_bit_alu_1_zf;
  wire [2:0] control_1_aluop_2_0;
  wire [3:0] datamemory_1_write_data__registers, instruction_memory_1_instruction_7_4,
       instruction_memory_1_last4_3_0, instruction_memory_1_opcode__15_12,
       instruction_memory_1_src_reg_1_11_8, n4_bit_alu_1_f, register_file_1_r1_data, register_file_1_r2_data;
  wire [7:0] address_1_pcin, instruction_memory_1_pcout;

  // Probe on instruction_memory_1_pcout
  Address address_1 (
    .PCIN(address_1_pcin), .Reg_2(instruction_memory_1_instruction_7_4), .PCOUT(instruction_memory_1_pcout),
    .Reg_3(instruction_memory_1_last4_3_0), .beq(control_1_beq_5), .bneq(control_1_bneq_4),
    .zf(n4_bit_alu_1_zf), .jump(control_1_jump_11), .Reg_1(instruction_memory_1_src_reg_1_11_8));  // open: out_10, out_11
  Instruction_Memory instruction_memory_1 (
    .PC(address_1_pcin), .Opcode__15_12(instruction_memory_1_opcode__15_12),
    .Src_Reg_1_11_8(instruction_memory_1_src_reg_1_11_8),
    .Instruction_7_4(instruction_memory_1_instruction_7_4), .last4_3_0(instruction_memory_1_last4_3_0),
    .clk(clock_1_out), .reset(RESET), .pcout(instruction_memory_1_pcout));  // open: testout, Jump__11_4
  control control_1 (
    .opcode(instruction_memory_1_opcode__15_12), .aluop_2_0(control_1_aluop_2_0),
    .alusrc_3(control_1_alusrc_3), .bneq_4(control_1_bneq_4), .beq_5(control_1_beq_5),
    .memtoReg_6(control_1_memtoreg_6), .memWrit_7(control_1_memwrit_7), .memRead_8(control_1_memread_8),
    .RegWrite_9(control_1_regwrite_9), .RegDst_10(control_1_regdst_10), .jump_11(control_1_jump_11));  // open: testout
  Clock clock_1 (.out(clock_1_out));
  _4_bit_ALU u_4_bit_alu_1 (
    .A(register_file_1_r1_data), .Read_Data2(register_file_1_r2_data), .ALUop(control_1_aluop_2_0),
    .ZF(n4_bit_alu_1_zf), .F(n4_bit_alu_1_f), .Reg_3(instruction_memory_1_last4_3_0),
    .ALU_SRC(control_1_alusrc_3));  // open: Overflow, Negative, out_10
  // Probe on control_1_aluop_2_0
  // Probe on register_file_1_r1_data
  // Probe on n4_bit_alu_1_f
  Register_File register_file_1 (
    .R1_num(instruction_memory_1_src_reg_1_11_8), .R2_num(instruction_memory_1_instruction_7_4),
    .Write_Data(datamemory_1_write_data__registers), .RegWrite(control_1_regwrite_9), .Clk(clock_1_out),
    .R3_num(instruction_memory_1_last4_3_0), .R1_Data(register_file_1_r1_data),
    .R2_Data(register_file_1_r2_data), .out_11({t4, t3, t2, t1, t0, Z}), .clear_reg(RESET),
    .ResDST(control_1_regdst_10));
  // Probe on register_file_1_r2_data
  // Probe on datamemory_1_write_data__registers
  dataMemory datamemory_1 (
    .alurRsult(n4_bit_alu_1_f), .WriteData(register_file_1_r2_data), .clk(clock_1_out),
    .MemWrite(control_1_memwrit_7), .MemRead(control_1_memread_8), .ram_cler(RESET),
    .Write_Data__Registers(datamemory_1_write_data__registers), .MemToReg(control_1_memtoreg_6));
endmodule

module _4_bit_ALU (
  input  [3:0] A,
  input  [3:0] Read_Data2,
  input  [3:0] Reg_3,
  input  [2:0] ALUop,
  input  ALU_SRC,
  output ZF,
  output Overflow,
  output Negative,
  output [3:0] F,
  output [3:0] out_10
);

  wire n7432_1_p3, n7432_1_p6, n7432_1_p11;
  wire [3:0] adder_1_out, and_1_out, multiplexer_1_out, nor_1_out, or_1_out, shifter_2_out, subtractor_1_out;

  Multiplexer #(.width(4), .enable("false")) multiplexer_1 (
    .in0(Read_Data2), .in1(Reg_3), .out(multiplexer_1_out), .sel(ALU_SRC));
  Adder #(.width(4)) adder_1 (.a(A), .b(multiplexer_1_out), .out(adder_1_out), .cin(1'b0), .cout(Overflow));
  Subtractor #(.width(4)) subtractor_1 (
    .a(A), .b(multiplexer_1_out), .out(subtractor_1_out), .bin(1'b0), .bout(Negative));
  assign and_1_out = A & multiplexer_1_out;  // AND_Gate and_1, 4 bits wide
  assign or_1_out = A | multiplexer_1_out;  // OR_Gate or_1, 4 bits wide
  assign nor_1_out = ~(A | multiplexer_1_out);  // NOR_Gate nor_1, 4 bits wide
  Shifter #(.width(4), .shift("lr")) shifter_1 (.in(A), .\dist (multiplexer_1_out[1:0]), .out(out_10));
  Shifter #(.width(4)) shifter_2 (.in(A), .\dist (multiplexer_1_out[1:0]), .out(shifter_2_out));
  Multiplexer #(.select(3), .width(4), .enable("false")) multiplexer_2 (
    .in0(adder_1_out), .in1(subtractor_1_out), .in2(and_1_out), .in3(or_1_out), .in4(shifter_2_out),
    .in5(out_10), .in6(nor_1_out), .in7(4'b0000), .out(F), .sel(ALUop));
  // _7432 7432_1: pin names not known; wires that end beside it: F[0], F[1], n7432_1_p3, n7432_1_p3, F[2], n7432_1_p6, 1'b0, 1'b1, n7432_1_p6, F[3], n7432_1_p11
  // _7404 7404_1: pin names not known; wires that end beside it: n7432_1_p11, ZF, 1'b0, 1'b1

  // Notes on the sheet:
  //   B
endmodule

module Instruction_Memory (
  input  [7:0] PC,
  input  clk,
  input  reset,
  output [7:0] pcout,
  output [3:0] Opcode__15_12,
  output [3:0] Src_Reg_1_11_8,
  output [15:0] testout,
  output [3:0] Instruction_7_4,
  output [7:0] Jump__11_4,
  output [3:0] last4_3_0
);

  Register #(.trigger("falling")) register_1 (.D(PC), .en(1'b1), .Q(pcout), .clk(clk), .clr(reset));
  ROM #(.dataWidth(16)) rom_1 (
    .addr(pcout), .data({Opcode__15_12, Jump__11_4[7:4], Instruction_7_4, last4_3_0}));  // open: sel

  assign Jump__11_4[3:0] = Instruction_7_4;
  assign Src_Reg_1_11_8 = Jump__11_4[7:4];
  assign testout = {Opcode__15_12, Jump__11_4[7:4], Instruction_7_4, last4_3_0};

  // Notes on the sheet:
  //   contents of rom_1 (hex, n*v repeats v):
  //   23 803e e231 9234 5135 7323 a331 2341 d140 1441 6334 d130 c131 a552 f531 1551 3225 f324 d140 b138
endmodule

module control (
  input  [3:0] opcode,
  output [11:0] testout,
  output [2:0] aluop_2_0,
  output alusrc_3,
  output bneq_4,
  output beq_5,
  output memtoReg_6,
  output memWrit_7,
  output memRead_8,
  output RegWrite_9,
  output RegDst_10,
  output jump_11
);

  ROM #(.addrWidth(4), .dataWidth(12)) rom_1 (
    .addr(opcode),
    .data({jump_11, RegDst_10, RegWrite_9, memRead_8, memWrit_7, memtoReg_6, beq_5, bneq_4, alusrc_3, aluop_2_0}));  // open: sel

  assign testout = {jump_11, RegDst_10, RegWrite_9, memRead_8, memWrit_7, memtoReg_6, beq_5, bneq_4, alusrc_3, aluop_2_0};

  // Notes on the sheet:
  //   contents of rom_1 (hex, n*v repeats v):
  //   208 20c 21 20b 602 606 348 88 209 601 20d 11 603 800 600 20a
endmodule

module Register_File (
  input  [3:0] R1_num,
  input  [3:0] R2_num,
  input  [3:0] Write_Data,
  input  [3:0] R3_num,
  input  ResDST,
  input  RegWrite,
  input  Clk,
  input  clear_reg,
  output [3:0] R1_Data,
  output [3:0] R2_Data,
  output [23:0] out_11
);

  wire and_1_out, demultiplexer_1_out0, demultiplexer_1_out1, demultiplexer_1_out2, demultiplexer_1_out3,
       demultiplexer_1_out4, demultiplexer_1_out5;
  wire [3:0] multiplexer_1_out;

  and and_1 (and_1_out, RegWrite, Clk);
  Multiplexer #(.width(4), .disabled(0), .enable("false")) multiplexer_1 (
    .in0(R2_num), .in1(R3_num), .out(multiplexer_1_out), .sel(ResDST));
  Demultiplexer #(.select(3), .disabled(0), .enable("false")) demultiplexer_1 (
    .out0(demultiplexer_1_out0), .out1(demultiplexer_1_out1), .out2(demultiplexer_1_out2),
    .out3(demultiplexer_1_out3), .out4(demultiplexer_1_out4), .out5(demultiplexer_1_out5), .in(and_1_out),
    .sel(multiplexer_1_out[2:0]));  // open: out6, out7
  Register #(.width(4), .trigger("falling")) _0__zero (
    .D(4'b0000), .Q(out_11[3:0]), .clk(demultiplexer_1_out0), .clr(clear_reg));  // open: en
  Register #(.width(4), .trigger("falling")) t0 (
    .D(Write_Data), .Q(out_11[7:4]), .clk(demultiplexer_1_out1), .clr(clear_reg));  // open: en
  Register #(.width(4), .trigger("falling")) t1 (
    .D(Write_Data), .Q(out_11[11:8]), .clk(demultiplexer_1_out2), .clr(clear_reg));  // open: en
  Register #(.width(4), .trigger("falling")) t2 (
    .D(Write_Data), .Q(out_11[15:12]), .clk(demultiplexer_1_out3), .clr(clear_reg));  // open: en
  Register #(.width(4), .trigger("falling")) t3 (
    .D(Write_Data), .Q(out_11[19:16]), .clk(demultiplexer_1_out4), .clr(clear_reg));  // open: en
  Register #(.width(4), .trigger("falling")) t4 (
    .D(Write_Data), .Q(out_11[23:20]), .clk(demultiplexer_1_out5), .clr(clear_reg));  // open: en
  Multiplexer #(.select(3), .width(4), .disabled(0), .enable("false")) multiplexer_2 (
    .in0(out_11[3:0]), .in1(out_11[7:4]), .in2(out_11[11:8]), .in3(out_11[15:12]), .in4(out_11[19:16]),
    .in5(out_11[23:20]), .in6(4'b0000), .in7(4'b0000), .out(R1_Data), .sel(R1_num[2:0]));
  Multiplexer #(.select(3), .width(4), .disabled(0), .enable("false")) multiplexer_3 (
    .in0(out_11[3:0]), .in1(out_11[7:4]), .in2(out_11[11:8]), .in3(out_11[15:12]), .in4(out_11[19:16]),
    .in5(out_11[23:20]), .in6(4'b0000), .in7(4'b0000), .out(R2_Data), .sel(R2_num[2:0]));
endmodule

module dataMemory (
  input  [3:0] alurRsult,
  input  [3:0] WriteData,
  input  MemToReg,
  input  MemWrite,
  input  MemRead,
  input  clk,
  input  ram_cler,
  output [3:0] Write_Data__Registers
);

  wire [3:0] ram_1_data;

  RAM #(.addrWidth(4), .dataWidth(4), .bus("separate")) ram_1 (
    .addr(alurRsult), .din(WriteData), .data(ram_1_data), .str(MemWrite), .clk(clk), .ld(MemRead),
    .clr(ram_cler));  // open: sel
  Multiplexer #(.width(4), .disabled(0), .enable("false")) multiplexer_1 (
    .in0(alurRsult), .in1(ram_1_data), .out(Write_Data__Registers), .sel(MemToReg));
endmodule

module branch (
  input  beq,
  input  bneq,
  input  zf,
  output out_4
);

  wire n7404_1_p2, n7408_1_p3, n7408_1_p6;

  // _7404 7404_1: pin names not known; wires that end beside it: zf, n7404_1_p2
  // _7408 7408_1: pin names not known; wires that end beside it: beq, zf, n7408_1_p3, bneq, n7404_1_p2, n7408_1_p6
  // _7432 7432_1: pin names not known; wires that end beside it: n7408_1_p3, n7408_1_p6, out_4
endmodule

module Address (
  input  jump,
  input  [3:0] Reg_2,
  input  [3:0] Reg_1,
  input  [7:0] PCOUT,
  input  [3:0] Reg_3,
  input  beq,
  input  bneq,
  input  zf,
  output [7:0] PCIN,
  output [7:0] out_10,
  output [7:0] out_11
);

  wire branch_1_out_4;
  wire [7:0] adder_1_out, adder_2_out, multiplexer_1_out;

  Adder adder_1 (.a(PCOUT), .b(8'h1), .out(adder_1_out));  // open: cin, cout
  assign out_11 = {{4{Reg_3[3]}}, Reg_3};  // Bit_Extender bit_extender_1
  Adder adder_2 (.a(adder_1_out), .b(out_11), .out(adder_2_out));  // open: cin, cout
  Multiplexer #(.width(8), .disabled(0), .enable("false")) multiplexer_1 (
    .in0(adder_1_out), .in1(adder_2_out), .out(multiplexer_1_out), .sel(branch_1_out_4));
  branch branch_1 (.out_4(branch_1_out_4), .beq(beq), .bneq(bneq), .zf(zf));
  Multiplexer #(.width(8), .disabled(0), .enable("false")) multiplexer_2 (
    .in0(multiplexer_1_out), .in1({Reg_1, Reg_2}), .out(PCIN), .sel(jump));

  assign out_10 = {Reg_1, Reg_2};
endmodule
