// Logisim project MIPS-4bit-G2.circ as structural Verilog: 7 circuits, main circuit main
// 1
module main (
  input  Reset,
  output [7:0] pcout,
  output [3:0] out_3,
  output [3:0] zero,
  output [3:0] t0,
  output [3:0] t1,
  output [3:0] t2,
  output [3:0] t3,
  output [3:0] t4
);

  wire branch_1_out_4, clock_1_out, control_1_alusrc_3, control_1_beq_5, control_1_bneq_4, control_1_jump_11,
       control_1_memread_8, control_1_memtoreg_6, control_1_memwrit_7, control_1_regdst_10,
       control_1_regwrite_9, n4_bit_alu_1_zf;
  wire [2:0] control_1_aluop_2_0;
  wire [3:0] datamemory_1_readdata, instruction_memory_1_instruction_7_4, instruction_memory_1_last4_3_0,
       instruction_memory_1_opcode__15_12, instruction_memory_1_src_reg_1_11_8, multiplexer_1_out,
       multiplexer_2_out, multiplexer_5_out, register_file_1_r1_data, register_file_1_r2_data;
  wire [7:0] adder_1_out, adder_2_out, bit_extender_1_out, instruction_memory_1_jump__11_4,
       multiplexer_3_out, multiplexer_4_out;

  Instruction_Memory instruction_memory_1 (
    .PC(multiplexer_3_out), .Opcode__15_12(instruction_memory_1_opcode__15_12),
    .Src_Reg_1_11_8(instruction_memory_1_src_reg_1_11_8),
    .Instruction_7_4(instruction_memory_1_instruction_7_4), .Jump__11_4(instruction_memory_1_jump__11_4),
    .last4_3_0(instruction_memory_1_last4_3_0), .clk(clock_1_out), .reset(Reset), .pcout(pcout));  // open: testout
  Clock clock_1 (.out(clock_1_out));
  Adder adder_1 (.a(pcout), .b(8'h1), .out(adder_1_out));  // open: cin, cout
  control control_1 (
    .opcode(instruction_memory_1_opcode__15_12), .aluop_2_0(control_1_aluop_2_0),
    .alusrc_3(control_1_alusrc_3), .bneq_4(control_1_bneq_4), .beq_5(control_1_beq_5),
    .memtoReg_6(control_1_memtoreg_6), .memWrit_7(control_1_memwrit_7), .memRead_8(control_1_memread_8),
    .RegWrite_9(control_1_regwrite_9), .RegDst_10(control_1_regdst_10), .jump_11(control_1_jump_11));  // open: testout
  Multiplexer #(.width(4), .disabled(0), .enable("false")) multiplexer_1 (
    .in0(instruction_memory_1_instruction_7_4), .in1(instruction_memory_1_last4_3_0),
    .out(multiplexer_1_out), .sel(control_1_regdst_10));
  assign bit_extender_1_out = {{4{instruction_memory_1_last4_3_0[3]}}, instruction_memory_1_last4_3_0};  // Bit_Extender bit_extender_1
  Register_File register_file_1 (
    .R1_num(instruction_memory_1_src_reg_1_11_8), .R2_num(instruction_memory_1_instruction_7_4),
    .Write_Data(multiplexer_5_out), .RegWrite(control_1_regwrite_9), .Clk(clock_1_out),
    .WriteResistor(multiplexer_1_out), .R1_Data(register_file_1_r1_data), .R2_Data(register_file_1_r2_data),
    .out_10({t4, t3, t2, t1, t0, zero}), .clear_reg(Reset));
  Adder adder_2 (.a(adder_1_out), .b(bit_extender_1_out), .out(adder_2_out));  // open: cin, cout
  Multiplexer #(.width(4), .disabled(0), .enable("false")) multiplexer_2 (
    .in0(register_file_1_r2_data), .in1(instruction_memory_1_last4_3_0), .out(multiplexer_2_out),
    .sel(control_1_alusrc_3));
  branch branch_1 (.out_4(branch_1_out_4), .beq(control_1_beq_5), .bneq(control_1_bneq_4), .zf(n4_bit_alu_1_zf));
  _4_bit_ALU u_4_bit_alu_1 (
    .A(register_file_1_r1_data), .B(multiplexer_2_out), .ALUop(control_1_aluop_2_0), .ZF(n4_bit_alu_1_zf),
    .F(out_3));  // open: Overflow, Negative
  Multiplexer #(.width(8), .disabled(0), .enable("false")) multiplexer_3 (
    .in0(multiplexer_4_out), .in1(instruction_memory_1_jump__11_4), .out(multiplexer_3_out),
    .sel(control_1_jump_11));
  Multiplexer #(.width(8), .disabled(0), .enable("false")) multiplexer_4 (
    .in0(adder_1_out), .in1(adder_2_out), .out(multiplexer_4_out), .sel(branch_1_out_4));
  dataMemory datamemory_1 (
    .alurRsult(out_3), .WriteData(register_file_1_r2_data), .ReadData(datamemory_1_readdata),
    .clk(clock_1_out), .MemWrite(control_1_memwrit_7), .MemRead(control_1_memread_8), .ram_cler(Reset));
  Multiplexer #(.width(4), .disabled(0), .enable("false")) multiplexer_5 (
    .in0(out_3), .in1(datamemory_1_readdata), .out(multiplexer_5_out), .sel(control_1_memtoreg_6));
endmodule

module _4_bit_ALU (
  input  [3:0] A,
  input  [3:0] B,
  input  [2:0] ALUop,
  output ZF,
  output Overflow,
  output Negative,
  output [3:0] F
);

  wire n7432_1_p3, n7432_1_p6, n7432_1_p11;
  wire [3:0] adder_1_out, and_1_out, nor_1_out, or_1_out, shifter_1_out, shifter_2_out, subtractor_1_out;

  Adder #(.width(4)) adder_1 (.a(A), .b(B), .out(adder_1_out), .cin(1'b0), .cout(Overflow));
  Subtractor #(.width(4)) subtractor_1 (.a(A), .b(B), .out(subtractor_1_out), .bin(1'b0), .bout(Negative));
  assign and_1_out = A & B;  // AND_Gate and_1, 4 bits wide
  assign or_1_out = A | B;  // OR_Gate or_1, 4 bits wide
  assign nor_1_out = ~(A | B);  // NOR_Gate nor_1, 4 bits wide
  Shifter #(.width(4), .shift("lr")) shifter_1 (.in(A), .\dist (B[1:0]), .out(shifter_1_out));
  Shifter #(.width(4)) shifter_2 (.in(A), .\dist (B[1:0]), .out(shifter_2_out));
  Multiplexer #(.select(3), .width(4), .enable("false")) multiplexer_1 (
    .in0(adder_1_out), .in1(subtractor_1_out), .in2(and_1_out), .in3(or_1_out), .in4(shifter_2_out),
    .in5(shifter_1_out), .in6(nor_1_out), .in7(4'b0000), .out(F), .sel(ALUop));
  // _7432 7432_1: pin names not known; wires that end beside it: F[0], F[1], n7432_1_p3, n7432_1_p3, F[2], n7432_1_p6, 1'b0, 1'b1, n7432_1_p6, F[3], n7432_1_p11
  // _7404 7404_1: pin names not known; wires that end beside it: n7432_1_p11, ZF, 1'b0, 1'b1
endmodule

module Instruction_Memory (
  input  [7:0] PC,
  input  clk,
  input  reset,
  output [7:0] pcout,
  output [3:0] Opcode__15_12,
  output [3:0] Src_Reg_1_11_8,
  output [15:0] testout,
  output [3:0] Instruction_7_4,
  output [7:0] Jump__11_4,
  output [3:0] last4_3_0
);

  Register #(.trigger("falling")) register_1 (.D(PC), .en(1'b1), .Q(pcout), .clk(clk), .clr(reset));
  ROM #(.dataWidth(16)) rom_1 (
    .addr(pcout), .data({Opcode__15_12, Jump__11_4[7:4], Instruction_7_4, last4_3_0}));  // open: sel

  assign Jump__11_4[3:0] = Instruction_7_4;
  assign Src_Reg_1_11_8 = Jump__11_4[7:4];
  assign testout = {Opcode__15_12, Jump__11_4[7:4], Instruction_7_4, last4_3_0};

  // Notes on the sheet:
  //   contents of rom_1 (hex, n*v repeats v):
  //   23 803e e231 9234 5135 7323 a331 2341 d140 1441 6334 d130 c131 a552 f531 1551 3225 f324 d140 b138
endmodule

module control (
  input  [3:0] opcode,
  output [11:0] testout,
  output [2:0] aluop_2_0,
  output alusrc_3,
  output bneq_4,
  output beq_5,
  output memtoReg_6,
  output memWrit_7,
  output memRead_8,
  output RegWrite_9,
  output RegDst_10,
  output jump_11
);

  ROM #(.addrWidth(4), .dataWidth(12)) rom_1 (
    .addr(opcode),
    .data({jump_11, RegDst_10, RegWrite_9, memRead_8, memWrit_7, memtoReg_6, beq_5, bneq_4, alusrc_3, aluop_2_0}));  // open: sel

  assign testout = {jump_11, RegDst_10, RegWrite_9, memRead_8, memWrit_7, memtoReg_6, beq_5, bneq_4, alusrc_3, aluop_2_0};

  // Notes on the sheet:
  //   contents of rom_1 (hex, n*v repeats v):
  //   208 20c 21 20b 602 606 348 88 209 601 20d 11 603 800 600 20a
endmodule

module Register_File (
  input  [3:0] R1_num,
  input  [3:0] R2_num,
  input  [3:0] Write_Data,
  input  RegWrite,
  input  Clk,
  input  [3:0] WriteResistor,
  input  clear_reg,
  output [3:0] R1_Data,
  output [3:0] R2_Data,
  output [23:0] out_10
);

  wire and_1_out, demultiplexer_1_out0, demultiplexer_1_out1, demultiplexer_1_out2, demultiplexer_1_out3,
       demultiplexer_1_out4, demultiplexer_1_out5;

  and and_1 (and_1_out, RegWrite, Clk);
  Demultiplexer #(.select(3), .disabled(0), .enable("false")) demultiplexer_1 (
    .out0(demultiplexer_1_out0), .out1(demultiplexer_1_out1), .out2(demultiplexer_1_out2),
    .out3(demultiplexer_1_out3), .out4(demultiplexer_1_out4), .out5(demultiplexer_1_out5), .in(and_1_out),
    .sel(WriteResistor[2:0]));  // open: out6, out7
  Register #(.width(4), .trigger("falling")) _0__zero (
    .D(4'b0000), .Q(out_10[3:0]), .clk(demultiplexer_1_out0), .clr(clear_reg));  // open: en
  Register #(.width(4), .trigger("falling")) t0 (
    .D(Write_Data), .Q(out_10[7:4]), .clk(demultiplexer_1_out1), .clr(clear_reg));  // open: en
  Register #(.width(4), .trigger("falling")) t1 (
    .D(Write_Data), .Q(out_10[11:8]), .clk(demultiplexer_1_out2), .clr(clear_reg));  // open: en
  Register #(.width(4), .trigger("falling")) t2 (
    .D(Write_Data), .Q(out_10[15:12]), .clk(demultiplexer_1_out3), .clr(clear_reg));  // open: en
  Register #(.width(4), .trigger("falling")) t3 (
    .D(Write_Data), .Q(out_10[19:16]), .clk(demultiplexer_1_out4), .clr(clear_reg));  // open: en
  Register #(.width(4), .trigger("falling")) t4 (
    .D(Write_Data), .Q(out_10[23:20]), .clk(demultiplexer_1_out5), .clr(clear_reg));  // open: en
  Multiplexer #(.select(3), .width(4), .disabled(0), .enable("false")) multiplexer_1 (
    .in0(out_10[3:0]), .in1(out_10[7:4]), .in2(out_10[11:8]), .in3(out_10[15:12]), .in4(out_10[19:16]),
    .in5(out_10[23:20]), .in6(4'b0000), .in7(4'b0000), .out(R1_Data), .sel(R1_num[2:0]));
  Multiplexer #(.select(3), .width(4), .disabled(0), .enable("false")) multiplexer_2 (
    .in0(out_10[3:0]), .in1(out_10[7:4]), .in2(out_10[11:8]), .in3(out_10[15:12]), .in4(out_10[19:16]),
    .in5(out_10[23:20]), .in6(4'b0000), .in7(4'b0000), .out(R2_Data), .sel(R2_num[2:0]));
endmodule

module dataMemory (
  input  [3:0] alurRsult,
  input  [3:0] WriteData,
  input  MemWrite,
  input  MemRead,
  input  clk,
  input  ram_cler,
  output [3:0] ReadData
);

  RAM #(.addrWidth(4), .dataWidth(4), .bus("separate")) ram_1 (
    .addr(alurRsult), .din(WriteData), .data(ReadData), .str(MemWrite), .clk(clk), .ld(MemRead),
    .clr(ram_cler));  // open: sel
endmodule

module branch (
  input  beq,
  input  bneq,
  input  zf,
  output out_4
);

  wire n7404_1_p2, n7408_1_p3, n7408_1_p6;

  // _7404 7404_1: pin names not known; wires that end beside it: zf, n7404_1_p2
  // _7408 7408_1: pin names not known; wires that end beside it: beq, zf, n7408_1_p3, bneq, n7404_1_p2, n7408_1_p6
  // _7432 7432_1: pin names not known; wires that end beside it: n7408_1_p3, n7408_1_p6, out_4
endmodule
